# Fritzing sketch analog (saved by Fritzing 0.9.3b)

parts:
  R1 = Photocell (LDR) [package=THT]
  R2 = Resistor [tolerance=±5% resistance=220 package=THT]
  WeMos_D1_Mini1 = wemosd1x

nets:
  N1: R1.pin_0, R2.Pin_1, WeMos_D1_Mini1.a0
  N2: R1.pin_1, WeMos_D1_Mini1.g
  N3: R2.Pin_0, WeMos_D1_Mini1.3v3
