# Fritzing sketch blink (saved by Fritzing 0.9.3b)

parts:
  WeMos_D1_Mini1 = wemosd1x
  LED1 = LED - 5mm [color="Red (633nm)" package="5 mm [THT]"]
  R1 = Resistor [tolerance=±5% resistance=220 package=THT]

nets:
  N1: WeMos_D1_Mini1.d5, R1.Pin_1
  GND: WeMos_D1_Mini1.g, LED1.cathode
  N2: LED1.anode, R1.Pin_0
