# Fritzing sketch servo (saved by Fritzing 0.9.3b)

parts:
  WeMos_D1_Mini1 = wemosd1x
  J1 = Basic Servo

nets:
  5V: WeMos_D1_Mini1.5v, J1.vcc
  N1: WeMos_D1_Mini1.d5, J1.pulse
  N2: WeMos_D1_Mini1.g, J1.gnd
