# Fritzing sketch tft (saved by Fritzing 0.9.3b)

parts:
  WeMos_D1_Mini1 = wemosd1x
  TFT2 = tft

nets:
  3.3V: WeMos_D1_Mini1.3v3, TFT2.connector1, TFT2.connector9
  N1: WeMos_D1_Mini1.d1, TFT2.connector8
  N2: WeMos_D1_Mini1.d2, TFT2.connector7
  N3: WeMos_D1_Mini1.d4, TFT2.connector5
  N4: WeMos_D1_Mini1.d5, TFT2.connector3
  N5: WeMos_D1_Mini1.d6, TFT2.connector2
  N6: WeMos_D1_Mini1.d7, TFT2.connector4
  GND: WeMos_D1_Mini1.g, TFT2.connector10
